# Fritzing sketch swc (saved by Fritzing 0.9.3b)
circuit board: 8.46667cm x 5.64444cm
perfboards: 1

parts:
  Part1 = ADS1115
  Raspberry_Pi_1 = Raspberry Pi 3 [part_number=RPI-3-V1.2]
  R1 = Resistor [tolerance=±5% resistance=330 package="0402 [SMD]"]
  R2 = Resistor [tolerance=±5% resistance=150 package="0402 [SMD]"]
  SWC2 = female pin header, 2 pins [form="♀ (female)"]
  SWC1 = female pin header, 2 pins [form="♀ (female)"]
  J3 = double row female pin header, 4 pins [form="♀ (female)"]

nets:
  3V3: Part1.VDD, Raspberry_Pi_1.3v3, Raspberry_Pi_1.3V3, R1.Pin_0, R2.Pin_0, J3.pin1
  GND: Part1.GND, Raspberry_Pi_1.GND, SWC2.pin1, SWC1.pin1, J3.pin2
  N1: Part1.SCL, Raspberry_Pi_1.GPIO3, J3.pin3
  N2: Part1.SDA, Raspberry_Pi_1.GPIO2, J3.pin4
  N3: R1.Pin_1, SWC1.pin2
  N4: R2.Pin_1, SWC2.pin2

custom parts:
  ADS1115: ADC ADS1115
